# Fritzing sketch SN74LVC1G3157DBVR-adapter (saved by Fritzing 0.9.3b)
circuit board: 1.9cm x 1.15cm
breadboards: 1

parts:
  SN74HC4067_D = CD4066 [package="DIP (Dual Inline) [THT]"]  # not connected
  SN74HC4067 = CD4066 [package="DIP (Dual Inline) [THT]"]
  SN74HC4067_C = CD4066 [package="DIP (Dual Inline) [THT]"]  # not connected
  SN74HC4067_PWR = CD4066 [package="DIP (Dual Inline) [THT]"]  # not connected
  SN74HC4067_A = CD4066 [package="DIP (Dual Inline) [THT]"]  # not connected
  SN74HC4067_B = CD4066 [package="DIP (Dual Inline) [THT]"]  # not connected
  IC1 = SN74LVC2G14DBVR [package=SOT23-6]
  IC2 = SN74LVC2G14DBVR [package=SOT23-6]
  IC3 = SN74LVC2G14DBVR [package=SOT23-6]
  IC4 = SN74LVC2G14DBVR [package=SOT23-6]

nets:
  N1: SN74HC4067.connector0, IC1.1A
  N2: SN74HC4067.connector1, IC1.2Y
  N3: SN74HC4067.connector2, IC2.1A
  N4: SN74HC4067.connector3, IC2.2Y
  N5: SN74HC4067.connector4, SN74HC4067.connector5, SN74HC4067.connector11, SN74HC4067.connector12, IC1.1Y, IC2.1Y, IC3.1Y, IC4.1Y
  GND: SN74HC4067.connector6, IC1.GND, IC1.2A, IC2.GND, IC2.2A, IC3.GND, IC3.2A, IC4.GND, IC4.2A
  N6: SN74HC4067.connector7, IC4.2Y
  N7: SN74HC4067.connector8, IC4.1A
  N8: SN74HC4067.connector9, IC3.2Y
  N9: SN74HC4067.connector10, IC3.1A
  VCC: SN74HC4067.connector13, IC1.VCC, IC2.VCC, IC3.VCC, IC4.VCC

custom parts:
  CD4066: CD4066B CMOS Quad Bilateral Switch with subparts.
  CD4066: CD4066B CMOS Quad Bilateral Switch with subparts.
  CD4066: CD4066B CMOS Quad Bilateral Switch with subparts.
  CD4066: CD4066B CMOS Quad Bilateral Switch with subparts.
  CD4066: CD4066B CMOS Quad Bilateral Switch with subparts.
  CD4066: CD4066B CMOS Quad Bilateral Switch with subparts.
