# Fritzing sketch prototypeV0.1-board1 (saved by Fritzing 0.9.3b)
circuit board: 3.69986cm x 12.6488cm
breadboards: 1

parts:
  36 = female pin header, 36 pins [form="♀ (female)"]
  37 = female pin header, 36 pins [form="♀ (female)"]
  37_2 = rounded female pin header, 36 pins [form="♀ (female rounded)"]
  36_2 = female pin header, 36 pins [form="♀ (female)"]

nets:
  N1: 36.pin1, 36_2.pin1
  N2: 36.pin2, 36_2.pin2
  N3: 36.pin3, 36_2.pin3
  N4: 36.pin4, 36_2.pin4
  N5: 36.pin5, 36_2.pin5
  N6: 36.pin6, 36_2.pin6
  N7: 36.pin7, 36_2.pin7
  N8: 36.pin8, 36_2.pin8
  N9: 36.pin9, 36_2.pin9
  N10: 36.pin10, 36_2.pin10
  N11: 36.pin11, 36_2.pin11
  N12: 36.pin12, 36_2.pin12
  N13: 36.pin13, 36_2.pin13
  N14: 36.pin14, 36_2.pin14
  N15: 36.pin15, 36_2.pin15
  N16: 36.pin16, 36_2.pin16
  N17: 36.pin17, 36_2.pin17
  N18: 36.pin18, 36_2.pin18
  N19: 36.pin19, 36_2.pin19
  N20: 36.pin20, 36_2.pin20
  N21: 36.pin21, 36_2.pin21
  N22: 36.pin22, 36_2.pin22
  N23: 36.pin23, 36_2.pin23
  N24: 36.pin24, 36_2.pin24
  N25: 36.pin25, 36_2.pin25
  N26: 36.pin26, 36_2.pin26
  N27: 36.pin27, 36_2.pin27
  N28: 36.pin28, 36_2.pin28
  N29: 36.pin29, 36_2.pin29
  N30: 36.pin30, 36_2.pin30
  N31: 36.pin31, 36_2.pin31
  N32: 36.pin32, 36_2.pin32
  N33: 36.pin33, 36_2.pin33
  N34: 36.pin34, 36_2.pin34
  N35: 36.pin35, 36_2.pin35
  N36: 36.pin36, 36_2.pin36
  N37: 37.pin1, 37_2.pin1
  N38: 37.pin2, 37_2.pin2
  N39: 37.pin3, 37_2.pin3
  N40: 37.pin4, 37_2.pin4
  N41: 37.pin5, 37_2.pin5
  N42: 37.pin6, 37_2.pin6
  N43: 37.pin7, 37_2.pin7
  N44: 37.pin8, 37_2.pin8
  N45: 37.pin9, 37_2.pin9
  N46: 37.pin10, 37_2.pin10
  N47: 37.pin11, 37_2.pin11
  N48: 37.pin12, 37_2.pin12
  N49: 37.pin13, 37_2.pin13
  N50: 37.pin14, 37_2.pin14
  N51: 37.pin15, 37_2.pin15
  N52: 37.pin16, 37_2.pin16
  N53: 37.pin17, 37_2.pin17
  N54: 37.pin18, 37_2.pin18
  N55: 37.pin19, 37_2.pin19
  N56: 37.pin20, 37_2.pin20
  N57: 37.pin21, 37_2.pin21
  N58: 37.pin22, 37_2.pin22
  N59: 37.pin23, 37_2.pin23
  N60: 37.pin24, 37_2.pin24
  N61: 37.pin25, 37_2.pin25
  N62: 37.pin26, 37_2.pin26
  N63: 37.pin27, 37_2.pin27
  N64: 37.pin28, 37_2.pin28
  N65: 37.pin29, 37_2.pin29
  N66: 37.pin30, 37_2.pin30
  N67: 37.pin31, 37_2.pin31
  N68: 37.pin32, 37_2.pin32
  N69: 37.pin33, 37_2.pin33
  N70: 37.pin34, 37_2.pin34
  N71: 37.pin35, 37_2.pin35
  N72: 37.pin36, 37_2.pin36
