# Fritzing sketch prototypeV0.1-board2 (saved by Fritzing 0.9.3b)
circuit board: 7.79185cm x 15.2276cm
breadboards: 1

parts:
  VCC/GND = female pin header, 2 pins [form="♀ (female)"]
  Console_A0-A14 = female pin header, 15 pins [form="♀ (female)"]
  Console_D7-D0 = female pin header, 8 pins [form="♀ (female)"]
  Console_F0-F2 = female pin header, 3 pins [form="♀ (female)"]
  Cart_D0-D7 = female pin header, 8 pins [form="♀ (female)"]
  Cartridge_A0-A14 = female pin header, 15 pins [form="♀ (female)"]
  Cart_F0-F2 = female pin header, 3 pins [form="♀ (female)"]
  Console_A0-A15 = female pin header, 15 pins [form="♀ (female)"]
  Cart_D0-D9 = female pin header, 8 pins [form="♀ (female)"]
  Cart_F0-F4 = female pin header, 3 pins [form="♀ (female)"]
  Cartridge_A0-A16 = female pin header, 15 pins [form="♀ (female)"]
  Console_F0-F3 = female pin header, 3 pins [form="♀ (female)"]
  Console_D0-D8 = female pin header, 8 pins [form="♀ (female)"]
  VCC/GND1 = female pin header, 2 pins [form="♀ (female)"]
  36 = female pin header, 36 pins [form="♀ (female)"]
  37 = rounded female pin header, 36 pins [form="♀ (female rounded)"]
  37_2 = female pin header, 36 pins [form="♀ (female)"]
  36_2 = female pin header, 36 pins [form="♀ (female)"]

nets:
  N1: VCC/GND.pin1, VCC/GND1.pin1, 36.pin36, 36_2.pin36
  N2: VCC/GND.pin2, VCC/GND1.pin2, 36.pin1, 36_2.pin1
  N3: Console_A0-A14.pin1, Console_A0-A15.pin1, 36_2.pin13
  N4: Console_A0-A14.pin2, Console_A0-A15.pin2, 36_2.pin12
  N5: Console_A0-A14.pin3, Console_A0-A15.pin3, 36_2.pin11
  N6: Console_A0-A14.pin4, Console_A0-A15.pin4, 36_2.pin10
  N7: Console_A0-A14.pin5, Console_A0-A15.pin5, 36_2.pin9
  N8: Console_A0-A14.pin6, Console_A0-A15.pin6, 36_2.pin8
  N9: Console_A0-A14.pin7, Console_A0-A15.pin7, 36_2.pin7
  N10: Console_A0-A14.pin8, Console_A0-A15.pin8, 36_2.pin6
  N11: Console_A0-A14.pin9, Console_A0-A15.pin9, 36_2.pin5
  N12: Console_A0-A14.pin10, Console_A0-A15.pin10, 36_2.pin4
  N13: Console_A0-A14.pin11, Console_A0-A15.pin11, 36_2.pin3
  N14: Console_A0-A14.pin12, Console_A0-A15.pin12, 36_2.pin2
  N15: Console_A0-A14.pin13, Console_A0-A15.pin13, 37_2.pin3
  N16: Console_A0-A14.pin14, Console_A0-A15.pin14, 37_2.pin4
  N17: Console_A0-A14.pin15, Console_A0-A15.pin15, 37_2.pin5
  N18: Console_D7-D0.pin1, Console_D0-D8.pin1, 37_2.pin6
  N19: Console_D7-D0.pin2, Console_D0-D8.pin2, 37_2.pin7
  N20: Console_D7-D0.pin3, Console_D0-D8.pin3, 37_2.pin8
  N21: Console_D7-D0.pin4, Console_D0-D8.pin4, 37_2.pin9
  N22: Console_D7-D0.pin5, Console_D0-D8.pin5, 37_2.pin10
  N23: Console_D7-D0.pin6, Console_D0-D8.pin6, 37_2.pin11
  N24: Console_D7-D0.pin7, Console_D0-D8.pin7, 37_2.pin12
  N25: Console_D7-D0.pin8, Console_D0-D8.pin8, 37_2.pin13
  N26: Console_F0-F2.pin1, Console_F0-F3.pin1, 37_2.pin2
  N27: Console_F0-F2.pin2, Console_F0-F3.pin2, 37_2.pin14
  N28: Console_F0-F2.pin3, Console_F0-F3.pin3, 36_2.pin14
  N29: Cart_D0-D7.pin1, Cart_D0-D9.pin1, 37.pin6
  N30: Cart_D0-D7.pin2, Cart_D0-D9.pin2, 37.pin7
  N31: Cart_D0-D7.pin3, Cart_D0-D9.pin3, 37.pin8
  N32: Cart_D0-D7.pin4, Cart_D0-D9.pin4, 37.pin9
  N33: Cart_D0-D7.pin5, Cart_D0-D9.pin5, 37.pin10
  N34: Cart_D0-D7.pin6, Cart_D0-D9.pin6, 37.pin11
  N35: Cart_D0-D7.pin7, Cart_D0-D9.pin7, 37.pin12
  N36: Cart_D0-D7.pin8, Cart_D0-D9.pin8, 37.pin13
  N37: Cartridge_A0-A14.pin1, Cartridge_A0-A16.pin1, 36.pin13
  N38: Cartridge_A0-A14.pin2, Cartridge_A0-A16.pin2, 36.pin12
  N39: Cartridge_A0-A14.pin3, Cartridge_A0-A16.pin3, 36.pin11
  N40: Cartridge_A0-A14.pin4, Cartridge_A0-A16.pin4, 36.pin10
  N41: Cartridge_A0-A14.pin5, Cartridge_A0-A16.pin5, 36.pin9
  N42: Cartridge_A0-A14.pin6, Cartridge_A0-A16.pin6, 36.pin8
  N43: Cartridge_A0-A14.pin7, Cartridge_A0-A16.pin7, 36.pin7
  N44: Cartridge_A0-A14.pin8, Cartridge_A0-A16.pin8, 36.pin6
  N45: Cartridge_A0-A14.pin9, Cartridge_A0-A16.pin9, 36.pin5
  N46: Cartridge_A0-A14.pin10, Cartridge_A0-A16.pin10, 36.pin4
  N47: Cartridge_A0-A14.pin11, Cartridge_A0-A16.pin11, 36.pin3
  N48: Cartridge_A0-A14.pin12, Cartridge_A0-A16.pin12, 36.pin2
  N49: Cartridge_A0-A14.pin13, Cartridge_A0-A16.pin13, 37.pin3
  N50: Cartridge_A0-A14.pin14, Cartridge_A0-A16.pin14, 37.pin4
  N51: Cartridge_A0-A14.pin15, Cartridge_A0-A16.pin15, 37.pin5
  N52: Cart_F0-F2.pin1, Cart_F0-F4.pin1, 37.pin2
  N53: Cart_F0-F2.pin2, Cart_F0-F4.pin2, 37.pin14
  N54: Cart_F0-F2.pin3, Cart_F0-F4.pin3, 36.pin14
  N55: 36.pin15, 36_2.pin15
  N56: 36.pin16, 36_2.pin16
  N57: 36.pin17, 36_2.pin17
  N58: 36.pin18, 36_2.pin18
  N59: 36.pin19, 36_2.pin19
  N60: 36.pin20, 36_2.pin20
  N61: 36.pin21, 36_2.pin21
  N62: 36.pin22, 36_2.pin22
  N63: 36.pin23, 36_2.pin23
  N64: 36.pin24, 36_2.pin24
  N65: 36.pin25, 36_2.pin25
  N66: 36.pin26, 36_2.pin26
  N67: 36.pin27, 36_2.pin27
  N68: 36.pin28, 36_2.pin28
  N69: 36.pin29, 36_2.pin29
  N70: 36.pin30, 36_2.pin30
  N71: 36.pin31, 36_2.pin31
  N72: 36.pin32, 36_2.pin32
  N73: 36.pin33, 36_2.pin33
  N74: 36.pin34, 36_2.pin34
  N75: 36.pin35, 36_2.pin35
  N76: 37.pin1, 37_2.pin1
  N77: 37.pin15, 37_2.pin15
  N78: 37.pin16, 37_2.pin16
  N79: 37.pin17, 37_2.pin17
  N80: 37.pin18, 37_2.pin18
  N81: 37.pin19, 37_2.pin19
  N82: 37.pin20, 37_2.pin20
  N83: 37.pin21, 37_2.pin21
  N84: 37.pin22, 37_2.pin22
  N85: 37.pin23, 37_2.pin23
  N86: 37.pin24, 37_2.pin24
  N87: 37.pin25, 37_2.pin25
  N88: 37.pin26, 37_2.pin26
  N89: 37.pin27, 37_2.pin27
  N90: 37.pin28, 37_2.pin28
  N91: 37.pin29, 37_2.pin29
  N92: 37.pin30, 37_2.pin30
  N93: 37.pin31, 37_2.pin31
  N94: 37.pin32, 37_2.pin32
  N95: 37.pin33, 37_2.pin33
  N96: 37.pin34, 37_2.pin34
  N97: 37.pin35, 37_2.pin35
  N98: 37.pin36, 37_2.pin36
