# Fritzing sketch prototypeV0.1-board4 (saved by Fritzing 0.9.3b)
circuit board: 6.18304cm x 15.0591cm
breadboards: 1

parts:
  VCC/GND = female pin header, 2 pins [form="♀ (female)"]
  F0-F2 = female pin header, 3 pins [form="♀ (female)"]
  A0-A14 = female pin header, 15 pins [form="♀ (female)"]
  D7-D0 = female pin header, 8 pins [form="♀ (female)"]
  BUS_Connect = female pin header, 2 pins [form="♀ (female)"]
  VCC/GND2 = female pin header, 2 pins [form="♀ (female)"]
  BUS_Connect2 = female pin header, 2 pins [form="♀ (female)"]
  F0-F4 = female pin header, 3 pins [form="♀ (female)"]
  A0-A16 = female pin header, 15 pins [form="♀ (female)"]
  D7-D2 = female pin header, 8 pins [form="♀ (female)"]
  Mod1 = Raspberry Pi Pico
  J1 = female pin header, 6 pins [form="♀ (female)"]
  J2 = male pin header, 2 pins [form="♂ (male)"]
  J3 = Piezo Speaker
  Q1 = npn-Powertransistor [package="TO220 [THT]"]
  R1 = Resistor [tolerance=±5% resistance=220 package=THT]
  J4 = female pin header, 8 pins [form="♀ (female)"]
  J5 = rounded female pin header, 8 pins [form="♀ (female rounded)"]
  J6 = rounded female pin header, 8 pins [form="♀ (female rounded)"]

nets:
  N1: VCC/GND.pin1, VCC/GND2.pin1, Mod1.pin_39, J5.pin8
  N2: VCC/GND.pin2, VCC/GND2.pin2, Mod1.pin_38, J1.pin1, Q1.base, J5.pin7
  N3: F0-F2.pin1, F0-F4.pin1, Mod1.pin_26
  N4: F0-F2.pin2, F0-F4.pin2, Mod1.pin_27
  N5: F0-F2.pin3, F0-F4.pin3, Mod1.pin_28
  N6: A0-A14.pin1, A0-A16.pin1, Mod1.pin_10
  N7: A0-A14.pin2, A0-A16.pin2, Mod1.pin_11
  N8: A0-A14.pin3, A0-A16.pin3, Mod1.pin_12
  N9: A0-A14.pin4, A0-A16.pin4, Mod1.pin_13
  N10: A0-A14.pin5, A0-A16.pin5, Mod1.pin_14
  N11: A0-A14.pin6, A0-A16.pin6, Mod1.pin_16
  N12: A0-A14.pin7, A0-A16.pin7, Mod1.pin_17
  N13: A0-A14.pin8, A0-A16.pin8, Mod1.pin_18
  N14: A0-A14.pin9, A0-A16.pin9, Mod1.pin_19
  N15: A0-A14.pin10, A0-A16.pin10, Mod1.pin_20
  N16: A0-A14.pin11, A0-A16.pin11, Mod1.pin_21
  N17: A0-A14.pin12, A0-A16.pin12, Mod1.pin_22
  N18: A0-A14.pin13, A0-A16.pin13, Mod1.pin_23
  N19: A0-A14.pin14, A0-A16.pin14, Mod1.pin_24
  N20: A0-A14.pin15, A0-A16.pin15, Mod1.pin_25
  N21: D7-D0.pin1, D7-D2.pin1, Mod1.pin_9
  N22: D7-D0.pin2, D7-D2.pin2, Mod1.pin_8
  N23: D7-D0.pin3, D7-D2.pin3, Mod1.pin_7
  N24: D7-D0.pin4, D7-D2.pin4, Mod1.pin_5
  N25: D7-D0.pin5, D7-D2.pin5, Mod1.pin_4
  N26: D7-D0.pin6, D7-D2.pin6, Mod1.pin_3
  N27: D7-D0.pin7, D7-D2.pin7, Mod1.pin_2
  N28: D7-D0.pin8, D7-D2.pin8, Mod1.pin_1
  N29: BUS_Connect.pin1, BUS_Connect2.pin1, J5.pin4
  N30: BUS_Connect.pin2, BUS_Connect2.pin2, J1.pin2, J2.pin1, J3.pin2, J5.pin6
  N31: Mod1.pin_32, J4.pin2, J6.pin2
  N32: Mod1.pin_33, J4.pin1, J6.pin1
  N33: Mod1.pin_36, J2.pin2
  N34: J1.pin3, J5.pin3
  N35: J1.pin4, J5.pin5
  N36: J1.pin5, J5.pin1
  N37: J1.pin6, J5.pin2
  N38: J3.pin1, Q1.collector
  N39: Q1.emitter, R1.Pin_1
  N40: R1.Pin_0, J4.pin3, J6.pin3
  N41: J4.pin4, J6.pin4
  N42: J4.pin5, J6.pin5
  N43: J4.pin6, J6.pin6
  N44: J4.pin7, J6.pin7
  N45: J4.pin8, J6.pin8

notes:
  3.3v
  0

custom parts:
  Raspberry Pi Pico: Raspberry Pi Pico. Based around the RP2040 microcontroller the Pico is a low cost microcontroller device bringing Raspberry Pi quality, cost, and easy of use to the microcontroller space. Jan 2021, Split part in to two versions: tht (this one) and SMD. This one will drill holes for a .1 in header in pcb to allow plugging in the module as well as providing pads to solder the module to the top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
