# Fritzing sketch prototypeV0.1-board3 (saved by Fritzing 0.9.3b)
circuit board: 8.21317cm x 15.2093cm
breadboards: 1

parts:
  VCC/GND = female pin header, 2 pins [form="♀ (female)"]
  Console_A0-A14 = female pin header, 15 pins [form="♀ (female)"]
  Console_D7-D0 = female pin header, 8 pins [form="♀ (female)"]
  Console_F0-F2 = female pin header, 3 pins [form="♀ (female)"]
  Cart_D7-D0 = female pin header, 8 pins [form="♀ (female)"]
  Cartridge_A0-A14 = female pin header, 15 pins [form="♀ (female)"]
  Cart_F0-F2 = female pin header, 3 pins [form="♀ (female)"]
  Console_A0-A15 = female pin header, 15 pins [form="♀ (female)"]
  Cart_D0-D9 = female pin header, 8 pins [form="♀ (female)"]
  Cart_F0-F4 = female pin header, 3 pins [form="♀ (female)"]
  Cartridge_A0-A14_2 = female pin header, 15 pins [form="♀ (female)"]
  Console_F0-F3 = female pin header, 3 pins [form="♀ (female)"]
  Console_D0-D8 = female pin header, 8 pins [form="♀ (female)"]
  VCC/GND1 = female pin header, 2 pins [form="♀ (female)"]
  VCC/GND_2 = female pin header, 2 pins [form="♀ (female)"]
  D7-D1 = female pin header, 8 pins [form="♀ (female)"]
  A0-A14 = female pin header, 15 pins [form="♀ (female)"]
  74HC4066 = CD4066 [package="DIP (Dual Inline) [THT]"]
  74HC4066_A = CD4066 [package="DIP (Dual Inline) [THT]"]  # not connected
  74HC4066_B = CD4066 [package="DIP (Dual Inline) [THT]"]  # not connected
  74HC4066_C = CD4066 [package="DIP (Dual Inline) [THT]"]  # not connected
  74HC4066_D = CD4066 [package="DIP (Dual Inline) [THT]"]  # not connected
  74HC4066_PWR = CD4066 [package="DIP (Dual Inline) [THT]"]  # not connected
  74HC4066_D_2 = CD4066 [package="DIP (Dual Inline) [THT]"]  # not connected
  74HC4066_PWR_2 = CD4066 [package="DIP (Dual Inline) [THT]"]  # not connected
  74HC4066_C_2 = CD4066 [package="DIP (Dual Inline) [THT]"]  # not connected
  74HC4066_A_2 = CD4066 [package="DIP (Dual Inline) [THT]"]  # not connected
  74HC4066_2 = CD4066 [package="DIP (Dual Inline) [THT]"]
  74HC4066_B_2 = CD4066 [package="DIP (Dual Inline) [THT]"]  # not connected
  74HC4066_A_3 = CD4066 [package="DIP (Dual Inline) [THT]"]  # not connected
  74HC4066_PWR_3 = CD4066 [package="DIP (Dual Inline) [THT]"]  # not connected
  74HC4066_B_3 = CD4066 [package="DIP (Dual Inline) [THT]"]  # not connected
  74HC4066_C_3 = CD4066 [package="DIP (Dual Inline) [THT]"]  # not connected
  74HC4066_3 = CD4066 [package="DIP (Dual Inline) [THT]"]
  74HC4066_D_3 = CD4066 [package="DIP (Dual Inline) [THT]"]  # not connected
  74HC4066_B_4 = CD4066 [package="DIP (Dual Inline) [THT]"]  # not connected
  74HC4066_A_4 = CD4066 [package="DIP (Dual Inline) [THT]"]  # not connected
  74HC4066_PWR_4 = CD4066 [package="DIP (Dual Inline) [THT]"]  # not connected
  74HC4066_C_4 = CD4066 [package="DIP (Dual Inline) [THT]"]  # not connected
  74HC4066_4 = CD4066 [package="DIP (Dual Inline) [THT]"]
  74HC4066_D_4 = CD4066 [package="DIP (Dual Inline) [THT]"]  # not connected
  74HC4066_PWR_5 = CD4066 [package="DIP (Dual Inline) [THT]"]  # not connected
  74HC4066_B_5 = CD4066 [package="DIP (Dual Inline) [THT]"]  # not connected
  74HC4066_A_5 = CD4066 [package="DIP (Dual Inline) [THT]"]  # not connected
  74HC4066_C_5 = CD4066 [package="DIP (Dual Inline) [THT]"]  # not connected
  74HC4066_5 = CD4066 [package="DIP (Dual Inline) [THT]"]
  74HC4066_D_5 = CD4066 [package="DIP (Dual Inline) [THT]"]  # not connected
  74HC4066_D_6 = CD4066 [package="DIP (Dual Inline) [THT]"]  # not connected
  74HC4066_PWR_6 = CD4066 [package="DIP (Dual Inline) [THT]"]  # not connected
  74HC4066_A_6 = CD4066 [package="DIP (Dual Inline) [THT]"]  # not connected
  74HC4066_C_6 = CD4066 [package="DIP (Dual Inline) [THT]"]  # not connected
  74HC4066_6 = CD4066 [package="DIP (Dual Inline) [THT]"]
  74HC4066_B_6 = CD4066 [package="DIP (Dual Inline) [THT]"]  # not connected
  74HC4066_B_7 = CD4066 [package="DIP (Dual Inline) [THT]"]  # not connected
  74HC4066_D_7 = CD4066 [package="DIP (Dual Inline) [THT]"]  # not connected
  74HC4066_A_7 = CD4066 [package="DIP (Dual Inline) [THT]"]  # not connected
  74HC4066_C_7 = CD4066 [package="DIP (Dual Inline) [THT]"]  # not connected
  74HC4066_7 = CD4066 [package="DIP (Dual Inline) [THT]"]
  74HC4066_PWR_7 = CD4066 [package="DIP (Dual Inline) [THT]"]  # not connected
  F0-F2 = female pin header, 3 pins [form="♀ (female)"]
  BUS_Connect = female pin header, 1 pin [form="♀ (female)"]

nets:
  N1: VCC/GND.pin1, VCC/GND1.pin1, VCC/GND_2.pin1, 74HC4066.connector13, 74HC4066_2.connector13, 74HC4066_3.connector13, 74HC4066_4.connector13, 74HC4066_5.connector13, 74HC4066_6.connector13, 74HC4066_7.connector13
  N2: VCC/GND.pin2, VCC/GND1.pin2, VCC/GND_2.pin2, 74HC4066.connector6, 74HC4066_2.connector6, 74HC4066_3.connector6, 74HC4066_4.connector6, 74HC4066_5.connector6, 74HC4066_6.connector6, 74HC4066_7.connector6
  N3: Console_A0-A14.pin1, Console_A0-A15.pin1, 74HC4066.connector0
  N4: Console_A0-A14.pin2, Console_A0-A15.pin2, 74HC4066.connector2
  N5: Console_A0-A14.pin3, Console_A0-A15.pin3, 74HC4066_2.connector0
  N6: Console_A0-A14.pin4, Console_A0-A15.pin4, 74HC4066_2.connector2
  N7: Console_A0-A14.pin5, Console_A0-A15.pin5, 74HC4066.connector10
  N8: Console_A0-A14.pin6, Console_A0-A15.pin6, 74HC4066.connector8
  N9: Console_A0-A14.pin7, Console_A0-A15.pin7, 74HC4066_2.connector10
  N10: Console_A0-A14.pin8, Console_A0-A15.pin8, 74HC4066_2.connector8
  N11: Console_A0-A14.pin9, Console_A0-A15.pin9, 74HC4066_3.connector0
  N12: Console_A0-A14.pin10, Console_A0-A15.pin10, 74HC4066_3.connector2
  N13: Console_A0-A14.pin11, Console_A0-A15.pin11, 74HC4066_4.connector0
  N14: Console_A0-A14.pin12, Console_A0-A15.pin12, 74HC4066_4.connector2
  N15: Console_A0-A14.pin13, Console_A0-A15.pin13, 74HC4066_3.connector10
  N16: Console_A0-A14.pin14, Console_A0-A15.pin14, 74HC4066_3.connector8
  N17: Console_A0-A14.pin15, Console_A0-A15.pin15, 74HC4066_4.connector10
  N18: Console_D7-D0.pin1, Console_D0-D8.pin1, 74HC4066_5.connector0
  N19: Console_D7-D0.pin2, Console_D0-D8.pin2, 74HC4066_5.connector2
  N20: Console_D7-D0.pin3, Console_D0-D8.pin3, 74HC4066_6.connector0
  N21: Console_D7-D0.pin4, Console_D0-D8.pin4, 74HC4066_6.connector2
  N22: Console_D7-D0.pin5, Console_D0-D8.pin5, 74HC4066_5.connector10
  N23: Console_D7-D0.pin6, Console_D0-D8.pin6, 74HC4066_5.connector8
  N24: Console_D7-D0.pin7, Console_D0-D8.pin7, 74HC4066_6.connector10
  N25: Console_D7-D0.pin8, Console_D0-D8.pin8, 74HC4066_6.connector8
  N26: Console_F0-F2.pin1, Console_F0-F3.pin1, 74HC4066_7.connector0
  N27: Console_F0-F2.pin2, Console_F0-F3.pin2, 74HC4066_7.connector2
  N28: Console_F0-F2.pin3, Console_F0-F3.pin3, 74HC4066_7.connector10
  N29: Cart_D7-D0.pin1, Cart_D0-D9.pin1, D7-D1.pin1, 74HC4066_5.connector1
  N30: Cart_D7-D0.pin2, Cart_D0-D9.pin2, D7-D1.pin2, 74HC4066_5.connector3
  N31: Cart_D7-D0.pin3, Cart_D0-D9.pin3, D7-D1.pin3, 74HC4066_6.connector1
  N32: Cart_D7-D0.pin4, Cart_D0-D9.pin4, D7-D1.pin4, 74HC4066_6.connector3
  N33: Cart_D7-D0.pin5, Cart_D0-D9.pin5, D7-D1.pin5, 74HC4066_5.connector9
  N34: Cart_D7-D0.pin6, Cart_D0-D9.pin6, D7-D1.pin6, 74HC4066_5.connector7
  N35: Cart_D7-D0.pin7, Cart_D0-D9.pin7, D7-D1.pin7, 74HC4066_6.connector9
  N36: Cart_D7-D0.pin8, Cart_D0-D9.pin8, D7-D1.pin8, 74HC4066_6.connector7
  N37: Cartridge_A0-A14.pin1, Cartridge_A0-A14_2.pin1, A0-A14.pin1, 74HC4066.connector1
  N38: Cartridge_A0-A14.pin2, Cartridge_A0-A14_2.pin2, A0-A14.pin2, 74HC4066.connector3
  N39: Cartridge_A0-A14.pin3, Cartridge_A0-A14_2.pin3, A0-A14.pin3, 74HC4066_2.connector1
  N40: Cartridge_A0-A14.pin4, Cartridge_A0-A14_2.pin4, A0-A14.pin4, 74HC4066_2.connector3
  N41: Cartridge_A0-A14.pin5, Cartridge_A0-A14_2.pin5, A0-A14.pin5, 74HC4066.connector9
  N42: Cartridge_A0-A14.pin6, Cartridge_A0-A14_2.pin6, A0-A14.pin6, 74HC4066.connector7
  N43: Cartridge_A0-A14.pin7, Cartridge_A0-A14_2.pin7, A0-A14.pin7, 74HC4066_2.connector9
  N44: Cartridge_A0-A14.pin8, Cartridge_A0-A14_2.pin8, A0-A14.pin8, 74HC4066_2.connector7
  N45: Cartridge_A0-A14.pin9, Cartridge_A0-A14_2.pin9, A0-A14.pin9, 74HC4066_3.connector1
  N46: Cartridge_A0-A14.pin10, Cartridge_A0-A14_2.pin10, A0-A14.pin10, 74HC4066_3.connector3
  N47: Cartridge_A0-A14.pin11, Cartridge_A0-A14_2.pin11, A0-A14.pin11, 74HC4066_4.connector1
  N48: Cartridge_A0-A14.pin12, Cartridge_A0-A14_2.pin12, A0-A14.pin12, 74HC4066_4.connector3
  N49: Cartridge_A0-A14.pin13, Cartridge_A0-A14_2.pin13, A0-A14.pin13, 74HC4066_3.connector9
  N50: Cartridge_A0-A14.pin14, Cartridge_A0-A14_2.pin14, A0-A14.pin14, 74HC4066_3.connector7
  N51: Cartridge_A0-A14.pin15, Cartridge_A0-A14_2.pin15, A0-A14.pin15, 74HC4066_4.connector9
  N52: Cart_F0-F2.pin1, Cart_F0-F4.pin1, 74HC4066_7.connector1, F0-F2.pin1
  N53: Cart_F0-F2.pin2, Cart_F0-F4.pin2, 74HC4066_7.connector3, F0-F2.pin2
  N54: Cart_F0-F2.pin3, Cart_F0-F4.pin3, 74HC4066_7.connector9, F0-F2.pin3
  N55: 74HC4066.connector4, 74HC4066.connector5, 74HC4066.connector11, 74HC4066.connector12, 74HC4066_2.connector4, 74HC4066_2.connector5, 74HC4066_2.connector11, 74HC4066_2.connector12, 74HC4066_3.connector4, 74HC4066_3.connector5, 74HC4066_3.connector11, 74HC4066_3.connector12, 74HC4066_4.connector4, 74HC4066_4.connector5, 74HC4066_4.connector11, 74HC4066_4.connector12, 74HC4066_5.connector4, 74HC4066_5.connector5, 74HC4066_5.connector11, 74HC4066_5.connector12, 74HC4066_6.connector4, 74HC4066_6.connector5, 74HC4066_6.connector11, 74HC4066_6.connector12, 74HC4066_7.connector4, 74HC4066_7.connector5, 74HC4066_7.connector11, 74HC4066_7.connector12, BUS_Connect.pin1

custom parts:
  CD4066: CD4066B CMOS Quad Bilateral Switch with subparts.
  CD4066: CD4066B CMOS Quad Bilateral Switch with subparts.
  CD4066: CD4066B CMOS Quad Bilateral Switch with subparts.
  CD4066: CD4066B CMOS Quad Bilateral Switch with subparts.
  CD4066: CD4066B CMOS Quad Bilateral Switch with subparts.
  CD4066: CD4066B CMOS Quad Bilateral Switch with subparts.
