# Fritzing sketch prototypeV0.2-board1 (saved by Fritzing 0.9.3b)
circuit board: 16.6cm x 13.6027cm
breadboards: 1

parts:
  37 = rounded female pin header, 36 pins [form="♀ (female rounded)"]
  36 = female pin header, 36 pins [form="♀ (female)"]
  Mod2 = Raspberry Pi Pico
  37_2 = Pad [width=1.5 height=4 connect=center]
  Pad68 = Pad [width=1.5 height=4 connect=center]
  Pad61 = Pad [width=1.5 height=4 connect=center]
  Pad67 = Pad [width=1.5 height=4 connect=center]
  Pad53 = Pad [width=1.5 height=4 connect=center]
  Pad64 = Pad [width=1.5 height=4 connect=center]
  Pad76 = Pad [width=1.5 height=4 connect=center]
  Pad85 = Pad [width=1.5 height=4 connect=center]
  Pad69 = Pad [width=1.5 height=4 connect=center]
  Pad80 = Pad [width=1.5 height=4 connect=center]
  Pad72 = Pad [width=1.5 height=4 connect=center]
  Pad60 = Pad [width=1.5 height=4 connect=center]
  Pad78 = Pad [width=1.5 height=4 connect=center]
  Pad82 = Pad [width=1.5 height=4 connect=center]
  Pad77 = Pad [width=1.5 height=4 connect=center]
  Pad79 = Pad [width=1.5 height=4 connect=center]
  Pad83 = Pad [width=1.5 height=4 connect=center]
  Pad52 = Pad [width=1.5 height=4 connect=center]
  Pad70 = Pad [width=1.5 height=4 connect=center]
  Pad58 = Pad [width=1.5 height=4 connect=center]
  Pad51 = Pad [width=1.5 height=4 connect=center]
  Pad66 = Pad [width=1.5 height=4 connect=center]
  Pad54 = Pad [width=1.5 height=4 connect=center]
  Pad73 = Pad [width=1.5 height=4 connect=center]
  Pad55 = Pad [width=1.5 height=4 connect=center]
  Pad81 = Pad [width=1.5 height=4 connect=center]
  Pad59 = Pad [width=1.5 height=4 connect=center]
  Pad65 = Pad [width=1.5 height=4 connect=center]
  Pad75 = Pad [width=1.5 height=4 connect=center]
  Pad62 = Pad [width=1.5 height=4 connect=center]
  Pad71 = Pad [width=1.5 height=4 connect=center]
  Pad74 = Pad [width=1.5 height=4 connect=center]
  Pad84 = Pad [width=1.5 height=4 connect=center]
  Pad56 = Pad [width=1.5 height=4 connect=center]
  Pad57 = Pad [width=1.5 height=4 connect=center]
  36_2 = Pad [width=1.5 height=4 connect=center]
  Pad20 = Pad [width=1.5 height=4 connect=center]
  Pad9 = Pad [width=1.5 height=4 connect=center]
  Pad10 = Pad [width=1.5 height=4 connect=center]
  Pad12 = Pad [width=1.5 height=4 connect=center]
  Pad6 = Pad [width=1.5 height=4 connect=center]
  Pad17 = Pad [width=1.5 height=4 connect=center]
  36_3 = Pad [width=1.5 height=4 connect=center]
  Pad34 = Pad [width=1.5 height=4 connect=center]
  Pad27 = Pad [width=1.5 height=4 connect=center]
  Pad18 = Pad [width=1.5 height=4 connect=center]
  Pad11 = Pad [width=1.5 height=4 connect=center]
  Pad4 = Pad [width=1.5 height=4 connect=center]
  Pad15 = Pad [width=1.5 height=4 connect=center]
  Pad48 = Pad [width=1.5 height=4 connect=center]
  Pad13 = Pad [width=1.5 height=4 connect=center]
  Pad16 = Pad [width=1.5 height=4 connect=center]
  Pad7 = Pad [width=1.5 height=4 connect=center]
  Pad21 = Pad [width=1.5 height=4 connect=center]
  Pad37 = Pad [width=1.5 height=4 connect=center]
  Pad3 = Pad [width=1.5 height=4 connect=center]
  Pad14 = Pad [width=1.5 height=4 connect=center]
  Pad25 = Pad [width=1.5 height=4 connect=center]
  Pad31 = Pad [width=1.5 height=4 connect=center]
  Pad23 = Pad [width=1.5 height=4 connect=center]
  Pad22 = Pad [width=1.5 height=4 connect=center]
  Pad38 = Pad [width=1.5 height=4 connect=center]
  Pad35 = Pad [width=1.5 height=4 connect=center]
  Pad19 = Pad [width=1.5 height=4 connect=center]
  Pad8 = Pad [width=1.5 height=4 connect=center]
  Pad39 = Pad [width=1.5 height=4 connect=center]
  Pad24 = Pad [width=1.5 height=4 connect=center]
  Pad46 = Pad [width=1.5 height=4 connect=center]
  Pad5 = Pad [width=1.5 height=4 connect=center]
  Pad49 = Pad [width=1.5 height=4 connect=center]
  Pad50 = Pad [width=1.5 height=4 connect=center]
  Pad36 = Pad [width=1.5 height=4 connect=center]
  SN74HC4066_D = CD4066 [package="DIP (Dual Inline) [THT]"]  # not connected
  SN74HC4066 = CD4066 [package="DIP (Dual Inline) [THT]"]
  SN74HC4066_C = CD4066 [package="DIP (Dual Inline) [THT]"]  # not connected
  SN74HC4066_PWR = CD4066 [package="DIP (Dual Inline) [THT]"]  # not connected
  SN74HC4066_A = CD4066 [package="DIP (Dual Inline) [THT]"]  # not connected
  SN74HC4066_B = CD4066 [package="DIP (Dual Inline) [THT]"]  # not connected
  SN74HC4066_D_2 = CD4066 [package="DIP (Dual Inline) [THT]"]  # not connected
  SN74HC4066_2 = CD4066 [package="DIP (Dual Inline) [THT]"]
  SN74HC4066_C_2 = CD4066 [package="DIP (Dual Inline) [THT]"]  # not connected
  SN74HC4066_PWR_2 = CD4066 [package="DIP (Dual Inline) [THT]"]
  SN74HC4066_A_2 = CD4066 [package="DIP (Dual Inline) [THT]"]  # not connected
  SN74HC4066_B_2 = CD4066 [package="DIP (Dual Inline) [THT]"]  # not connected
  SN74HC4066_D_3 = CD4066 [package="DIP (Dual Inline) [THT]"]  # not connected
  SN74HC4066_3 = CD4066 [package="DIP (Dual Inline) [THT]"]
  SN74HC4066_C_3 = CD4066 [package="DIP (Dual Inline) [THT]"]  # not connected
  SN74HC4066_PWR_3 = CD4066 [package="DIP (Dual Inline) [THT]"]  # not connected
  SN74HC4066_A_3 = CD4066 [package="DIP (Dual Inline) [THT]"]  # not connected
  SN74HC4066_B_3 = CD4066 [package="DIP (Dual Inline) [THT]"]  # not connected
  SN74HC4066_D_4 = CD4066 [package="DIP (Dual Inline) [THT]"]  # not connected
  SN74HC4066_4 = CD4066 [package="DIP (Dual Inline) [THT]"]
  SN74HC4066_C_4 = CD4066 [package="DIP (Dual Inline) [THT]"]  # not connected
  SN74HC4066_PWR_4 = CD4066 [package="DIP (Dual Inline) [THT]"]  # not connected
  SN74HC4066_A_4 = CD4066 [package="DIP (Dual Inline) [THT]"]  # not connected
  SN74HC4066_B_4 = CD4066 [package="DIP (Dual Inline) [THT]"]  # not connected
  SN74HC4066_D_5 = CD4066 [package="DIP (Dual Inline) [THT]"]  # not connected
  SN74HC4066_5 = CD4066 [package="DIP (Dual Inline) [THT]"]
  SN74HC4066_C_5 = CD4066 [package="DIP (Dual Inline) [THT]"]  # not connected
  SN74HC4066_PWR_5 = CD4066 [package="DIP (Dual Inline) [THT]"]  # not connected
  SN74HC4066_A_5 = CD4066 [package="DIP (Dual Inline) [THT]"]  # not connected
  SN74HC4066_B_5 = CD4066 [package="DIP (Dual Inline) [THT]"]  # not connected
  SN74HC4066_D_6 = CD4066 [package="DIP (Dual Inline) [THT]"]  # not connected
  SN74HC4066_6 = CD4066 [package="DIP (Dual Inline) [THT]"]
  SN74HC4066_C_6 = CD4066 [package="DIP (Dual Inline) [THT]"]  # not connected
  SN74HC4066_PWR_6 = CD4066 [package="DIP (Dual Inline) [THT]"]  # not connected
  SN74HC4066_A_6 = CD4066 [package="DIP (Dual Inline) [THT]"]  # not connected
  SN74HC4066_B_6 = CD4066 [package="DIP (Dual Inline) [THT]"]  # not connected
  SN74HC4066_D_7 = CD4066 [package="DIP (Dual Inline) [THT]"]  # not connected
  SN74HC4066_7 = CD4066 [package="DIP (Dual Inline) [THT]"]
  SN74HC4066_C_7 = CD4066 [package="DIP (Dual Inline) [THT]"]  # not connected
  SN74HC4066_PWR_7 = CD4066 [package="DIP (Dual Inline) [THT]"]  # not connected
  SN74HC4066_A_7 = CD4066 [package="DIP (Dual Inline) [THT]"]  # not connected
  SN74HC4066_B_7 = CD4066 [package="DIP (Dual Inline) [THT]"]  # not connected
  ESP32 = female pin header, 5 pins [form="♀ (female)"]

nets:
  N1: 37.pin1, 37_2.pad
  N2: 37.pin2, SN74HC4066.connector7
  N3: 37.pin3, SN74HC4066.connector9
  N4: 37.pin4, SN74HC4066.connector3
  N5: 37.pin5, SN74HC4066.connector1
  N6: 37.pin6, SN74HC4066_3.connector7
  N7: 37.pin7, SN74HC4066_3.connector9
  N8: 37.pin8, SN74HC4066_3.connector3
  N9: 37.pin9, SN74HC4066_3.connector1
  N10: 37.pin10, SN74HC4066_6.connector7
  N11: 37.pin11, SN74HC4066_6.connector9
  N12: 37.pin12, SN74HC4066_6.connector3
  N13: 37.pin13, SN74HC4066_6.connector1
  N14: 37.pin14, SN74HC4066_5.connector7
  N15: 37.pin15, Pad77.pad
  N16: 37.pin16, Pad79.pad
  N17: 37.pin17, Pad83.pad
  N18: 37.pin18, Pad52.pad
  N19: 37.pin19, Pad70.pad
  N20: 37.pin20, Pad58.pad
  N21: 37.pin21, Pad51.pad
  N22: 37.pin22, Pad66.pad
  N23: 37.pin23, Pad54.pad
  N24: 37.pin24, Pad73.pad
  N25: 37.pin25, Pad55.pad
  N26: 37.pin26, Pad81.pad
  N27: 37.pin27, Pad59.pad
  N28: 37.pin28, Pad65.pad
  N29: 37.pin29, Pad75.pad
  N30: 37.pin30, Pad62.pad
  N31: 37.pin31, Pad71.pad
  N32: 37.pin32, Pad74.pad
  N33: 37.pin33, Pad84.pad
  N34: 37.pin34, Pad56.pad
  N35: 37.pin35, Pad57.pad
  N36: 37.pin36, 36_2.pad
  N37: 36.pin1, Mod2.pin_38, Pad36.pad, SN74HC4066.connector6, SN74HC4066_2.connector6, SN74HC4066_PWR_2.pin7, SN74HC4066_3.connector6, SN74HC4066_4.connector6, SN74HC4066_5.connector6, SN74HC4066_6.connector6, SN74HC4066_7.connector6, ESP32.pin3
  N38: 36.pin2, SN74HC4066_2.connector7
  N39: 36.pin3, SN74HC4066_2.connector9
  N40: 36.pin4, SN74HC4066_2.connector3
  N41: 36.pin5, SN74HC4066_2.connector1
  N42: 36.pin6, SN74HC4066_4.connector7
  N43: 36.pin7, SN74HC4066_4.connector9
  N44: 36.pin8, SN74HC4066_4.connector3
  N45: 36.pin9, SN74HC4066_4.connector1
  N46: 36.pin10, SN74HC4066_7.connector7
  N47: 36.pin11, SN74HC4066_7.connector9
  N48: 36.pin12, SN74HC4066_7.connector3
  N49: 36.pin13, SN74HC4066_7.connector1
  N50: 36.pin14, SN74HC4066_5.connector3
  N51: 36.pin15, Pad18.pad
  N52: 36.pin16, Pad17.pad
  N53: 36.pin17, Pad16.pad
  N54: 36.pin18, Pad15.pad
  N55: 36.pin19, Pad22.pad
  N56: 36.pin20, Pad19.pad
  N57: 36.pin21, Pad20.pad
  N58: 36.pin22, Pad24.pad
  N59: 36.pin23, Pad14.pad
  N60: 36.pin24, Pad21.pad
  N61: 36.pin25, Pad25.pad
  N62: 36.pin26, Pad34.pad
  N63: 36.pin27, Pad35.pad
  N64: 36.pin28, Pad39.pad
  N65: 36.pin29, Pad38.pad
  N66: 36.pin30, Pad49.pad
  N67: 36.pin31, Pad31.pad
  N68: 36.pin32, Pad37.pad
  N69: 36.pin33, Pad27.pad
  N70: 36.pin34, Pad48.pad
  N71: 36.pin35, Pad46.pad
  N72: 36.pin36, Mod2.pin_39, 36_3.pad, SN74HC4066.connector13, SN74HC4066_2.connector13, SN74HC4066_3.connector13, SN74HC4066_4.connector13, SN74HC4066_5.connector13, SN74HC4066_6.connector13, SN74HC4066_7.connector13, ESP32.pin1
  N73: Mod2.pin_1, Pad78.pad, SN74HC4066_6.connector0
  N74: Mod2.pin_2, Pad60.pad, SN74HC4066_6.connector2
  N75: Mod2.pin_3, Pad72.pad, SN74HC4066_6.connector10
  N76: Mod2.pin_4, Pad80.pad, SN74HC4066_6.connector8
  N77: Mod2.pin_5, Pad69.pad, SN74HC4066_3.connector0
  N78: Mod2.pin_7, Pad85.pad, SN74HC4066_3.connector2
  N79: Mod2.pin_8, Pad76.pad, SN74HC4066_3.connector10
  N80: Mod2.pin_9, Pad64.pad, SN74HC4066_3.connector8
  N81: Mod2.pin_10, Pad13.pad, SN74HC4066_7.connector0
  N82: Mod2.pin_11, Pad9.pad, SN74HC4066_7.connector2
  N83: Mod2.pin_12, Pad12.pad, SN74HC4066_7.connector10
  N84: Mod2.pin_13, Pad10.pad, SN74HC4066_7.connector8
  N85: Mod2.pin_14, Pad8.pad, SN74HC4066_4.connector0
  N86: Mod2.pin_16, Pad11.pad, SN74HC4066_4.connector2
  N87: Mod2.pin_17, Pad7.pad, SN74HC4066_4.connector10
  N88: Mod2.pin_18, Pad6.pad, SN74HC4066_4.connector8
  N89: Mod2.pin_19, Pad5.pad, SN74HC4066_2.connector0
  N90: Mod2.pin_20, Pad4.pad, SN74HC4066_2.connector2
  N91: Mod2.pin_21, Pad3.pad, SN74HC4066_2.connector10
  N92: Mod2.pin_22, Pad50.pad, SN74HC4066_2.connector8
  N93: Mod2.pin_23, Pad61.pad, SN74HC4066.connector10
  N94: Mod2.pin_24, Pad67.pad, SN74HC4066.connector2
  N95: Mod2.pin_25, Pad53.pad, SN74HC4066.connector0
  N96: Mod2.pin_26, Pad68.pad, SN74HC4066.connector8
  N97: Mod2.pin_27, Pad82.pad, SN74HC4066_5.connector8
  N98: Mod2.pin_28, Pad23.pad, SN74HC4066_5.connector2
  N99: Mod2.pin_32, ESP32.pin5
  N100: Mod2.pin_33, ESP32.pin4
  N101: SN74HC4066.connector4, SN74HC4066.connector5, SN74HC4066.connector11, SN74HC4066.connector12, SN74HC4066_2.connector4, SN74HC4066_2.connector5, SN74HC4066_2.connector11, SN74HC4066_2.connector12, SN74HC4066_3.connector4, SN74HC4066_3.connector5, SN74HC4066_3.connector11, SN74HC4066_3.connector12, SN74HC4066_4.connector4, SN74HC4066_4.connector5, SN74HC4066_4.connector11, SN74HC4066_4.connector12, SN74HC4066_5.connector4, SN74HC4066_5.connector5, SN74HC4066_5.connector11, SN74HC4066_5.connector12, SN74HC4066_6.connector4, SN74HC4066_6.connector5, SN74HC4066_6.connector11, SN74HC4066_6.connector12, SN74HC4066_7.connector4, SN74HC4066_7.connector5, SN74HC4066_7.connector11, SN74HC4066_7.connector12, ESP32.pin2

notes:
  RA NES ADAPTER - Prototype v0.2
  Designed in Brazil - By Odelot & GH

custom parts:
  Raspberry Pi Pico: Raspberry Pi Pico. Based around the RP2040 microcontroller the Pico is a low cost microcontroller device bringing Raspberry Pi quality, cost, and easy of use to the microcontroller space. Jan 2021, Split part in to two versions: tht (this one) and SMD. This one will drill holes for a .1 in header in pcb to allow plugging in the module as well as providing pads to solder the module to the top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
  CD4066: CD4066B CMOS Quad Bilateral Switch with subparts.
  CD4066: CD4066B CMOS Quad Bilateral Switch with subparts.
  CD4066: CD4066B CMOS Quad Bilateral Switch with subparts.
  CD4066: CD4066B CMOS Quad Bilateral Switch with subparts.
  CD4066: CD4066B CMOS Quad Bilateral Switch with subparts.
  CD4066: CD4066B CMOS Quad Bilateral Switch with subparts.
