# Fritzing sketch prototypeV0.2-board2 (saved by Fritzing 0.9.3b)
circuit board: 4.4603cm x 6.37693cm
breadboards: 1

parts:
  J6 = rounded female pin header, 8 pins [form="♀ (female rounded)"]
  J5 = rounded female pin header, 8 pins [form="♀ (female rounded)"]
  J4 = female pin header, 8 pins [form="♀ (female)"]
  Reset = Pushbutton [package="[THT]"]
  10k = Resistor [tolerance=±5% resistance=10k package=THT]
  BC548 = NPN-Transistor [package="TO92 [THT]"]
  Buzzer = Buzzer 12mm [package=buzzer-12mm-ns]
  LCD = female pin header, 7 pins [form="♀ (female)"]
  J7 = female pin header, 5 pins [form="♀ (female)"]
  1k = Resistor [tolerance=±5% resistance=1k package=THT]

nets:
  N1: J6.pin1, J4.pin1, J7.pin2
  N2: J6.pin2, J4.pin2, J7.pin1
  N3: J6.pin3, J4.pin3, 1k.Pin_1
  N4: J6.pin4, J4.pin4
  N5: J6.pin5, J4.pin5, Reset.Pin_1, Reset.Pin_2, 10k.Pin_1
  N6: J6.pin6, J4.pin6
  N7: J6.pin7, J4.pin7
  N8: J6.pin8, J4.pin8
  N9: J5.pin1, LCD.pin5
  N10: J5.pin2, LCD.pin6
  N11: J5.pin3, LCD.pin3
  N12: J5.pin4, J7.pin4
  N13: J5.pin5, LCD.pin4
  N14: J5.pin6, 10k.Pin_0, Buzzer.1, LCD.pin2
  N15: J5.pin7, Reset.Pin_3, Reset.Pin_4, BC548.E, LCD.pin1, J7.pin3
  N16: J5.pin8, J7.pin5
  N17: BC548.B, 1k.Pin_0
  N18: BC548.C, Buzzer.2

notes:
  LCD GND
  ESP32 C3
  supermini
  USB
  5v BC GND Serial
